// Logisim project tl_failure.circ as structural Verilog: 1 circuit, main circuit main
module main (
  input  TA,
  input  TaL,
  input  TB,
  input  TbL
);

  wire and_1_out, and_2_out, clock_1_out, comparator_1_eq, comparator_2_eq, comparator_3_eq, comparator_4_eq,
       comparator_5_eq, comparator_6_eq, comparator_7_eq, comparator_8_eq, l0o_out, lo1_out, lol_out,
       loo_out, not_1_out, not_2_out, not_3_out, not_4_out, not_5_out, not_7_out, not_8_out, not_9_out,
       not_13_out, not_14_out, not_15_out, not_16_out, not_17_out, not_18_out, o10_out, olo_out, oo1_out,
       ool_out, or_1_out, or_3_out, or_4_out, or_5_out, or_14_out, or_15_out;
  wire [0:0] not_11_out;
  wire [1:0] not_12_out, or_9_out;
  wire [1:1] not_6_out, not_10_out;
  wire [2:0] d_ff_1_q, multiplexer_1_out, or_6_out, or_10_out;

  not not_1 (not_1_out, TB);
  not not_2 (not_2_out, TbL);
  not not_3 (not_3_out, TaL);
  and lol (lol_out, TbL, not_1_out);
  and loo (loo_out, TB, not_2_out);
  not not_4 (not_4_out, TA);
  not not_5 (not_5_out, TaL);
  or or_1 (or_1_out, TA, not_5_out, TB, TbL);
  not not_6 (not_6_out[1], TB);
  Clock clock_1 (.out(clock_1_out));
  // OR_Gate or_2 has open pins: in0=TA, in1=not_3_out, out=open
  and l0o (l0o_out, 1'b1, TB);
  and lo1 (lo1_out, 1'b1, TbL);
  or or_3 (or_3_out, loo_out, 1'b0);
  or or_4 (or_4_out, TbL, TB, not_4_out);
  not not_7 (not_7_out, TbL);
  or or_5 (or_5_out, not_7_out, TB);
  and oo1 (oo1_out, TA, 1'b1);
  or or_6 (or_6_out[0], lol_out, 1'b0);
  and o10 (o10_out, 1'b1, TaL);
  not not_8 (not_8_out, TaL);
  not not_9 (not_9_out, TA);
  not not_10 (not_10_out[1], or_4_out);
  not not_11 (not_11_out[0], or_1_out);
  or or_7 (not_12_out[1], or_5_out, 1'b0);
  D_Flip_Flop d_ff_1 (.D(multiplexer_1_out[0]), .clk(clock_1_out), .Q(d_ff_1_q[0]));  // open: Qn, preset, reset
  D_Flip_Flop d_ff_2 (.D(multiplexer_1_out[1]), .clk(clock_1_out), .Q(d_ff_1_q[1]));  // open: Qn, preset, reset
  D_Flip_Flop d_ff_3 (.D(multiplexer_1_out[2]), .clk(clock_1_out), .Q(d_ff_1_q[2]));  // open: Qn, preset, reset
  or or_8 (or_10_out[1], o10_out, 1'b0);
  and ool (ool_out, TA, not_8_out);
  or or_9 (or_9_out[0], ool_out, 1'b0);
  and olo (olo_out, TaL, not_9_out);
  not not_12 (not_12_out[0], not_12_out[1]);
  or or_10 (or_10_out[0], oo1_out, lo1_out);
  or or_11 (or_10_out[2], lo1_out, l0o_out);
  or or_12 (or_9_out[1], 1'b0, olo_out);
  or or_13 (or_6_out[2], or_6_out[0], or_3_out);
  Multiplexer #(.select(3), .width(3)) multiplexer_1 (
    .in0(or_10_out), .in1({1'b0, not_10_out[1], 1'b1}), .in2({2'b01, not_11_out[0]}), .in3({1'b0, or_9_out}),
    .in4({1'b1, not_12_out}), .in5({1'b1, not_6_out[1], 1'b0}), .in6({or_6_out[2], 1'b0, or_6_out[0]}),
    .out(multiplexer_1_out), .sel(d_ff_1_q));  // open: in7
  Comparator #(.width(3)) comparator_1 (.a(multiplexer_1_out), .b(3'b000), .eq(comparator_1_eq));  // open: gt, lt
  Comparator #(.width(3)) comparator_2 (.a(multiplexer_1_out), .b(3'b011), .eq(comparator_2_eq));  // open: gt, lt
  Comparator #(.width(3)) comparator_3 (.a(multiplexer_1_out), .b(3'b001), .eq(comparator_3_eq));  // open: gt, lt
  Comparator #(.width(3)) comparator_4 (.a(multiplexer_1_out), .b(3'b010), .eq(comparator_4_eq));  // open: gt, lt
  Comparator #(.width(3)) comparator_5 (.a(multiplexer_1_out), .b(3'b000), .eq(comparator_5_eq));  // open: gt, lt
  Comparator #(.width(3)) comparator_6 (.a(multiplexer_1_out), .b(3'b110), .eq(comparator_6_eq));  // open: gt, lt
  Comparator #(.width(3)) comparator_7 (.a(multiplexer_1_out), .b(3'b100), .eq(comparator_7_eq));  // open: gt, lt
  Comparator #(.width(3)) comparator_8 (.a(multiplexer_1_out), .b(3'b101), .eq(comparator_8_eq));  // open: gt, lt
  not not_13 (not_13_out, comparator_2_eq);
  not not_14 (not_14_out, comparator_3_eq);
  not not_15 (not_15_out, comparator_4_eq);
  not not_16 (not_16_out, comparator_8_eq);
  not not_17 (not_17_out, comparator_7_eq);
  not not_18 (not_18_out, comparator_6_eq);
  and and_1 (and_1_out, not_13_out, not_14_out, not_15_out);
  or or_14 (or_14_out, and_1_out, comparator_1_eq);
  LED A (.in(or_14_out));
  LED led_1 (.in(comparator_2_eq));
  LED led_2 (.in(comparator_3_eq));
  LED led_3 (.in(comparator_4_eq));
  or or_15 (or_15_out, comparator_5_eq, and_2_out);
  LED B (.in(or_15_out));
  LED led_4 (.in(comparator_6_eq));
  LED led_5 (.in(comparator_7_eq));
  LED led_6 (.in(comparator_8_eq));
  and and_2 (and_2_out, not_16_out, not_17_out, not_18_out);
endmodule
