// Logisim project vending_machine_ver1.circ as structural Verilog: 3 circuits, main circuit main
module main (
);

  wire and_1_out, and_2_out, and_3_out, and_4_out, Ba_out, Bb_out, Bc_out, beverage_button_1_out_8,
       button_1_out, clock_1_out, comparator_1_eq, comparator_1_gt, comparator_2_eq, comparator_3_eq,
       comparator_3_gt, comparator_4_eq, comparator_4_gt, comparator_5_eq, comparator_6_eq, comparator_7_eq,
       comparator_8_eq, comparator_9_eq, comparator_10_eq, d_ff_1_q, d_ff_2_q, d_ff_5_q, not_1_out, or_1_out,
       or_2_out, or_3_out, or_4_out, or_5_out, or_6_out, rgbled_1_p2, rgbled_1_p3, s_r_ff_1_q, Sc_out, Sp_out;
  wire [1:0] d_ff_3_q;
  wire [2:0] register_1_q_2;
  wire [7:0] counter_1_q;
  wire [12:0] register_1_q;
  wire [15:0] adder_1_out, beverage_button_1_out_7, multiplexer_1_out, multiplexer_2_out, multiplexer_3_out,
       multiplexer_4_out, subtractor_1_out;

  Button Ba (.out(Ba_out));
  Button Bb (.out(Bb_out));
  Button Bc (.out(Bc_out));
  Clock clock_1 (.out(clock_1_out));
  Button Sc (.out(Sc_out));
  Button Sp (.out(Sp_out));
  Counter #(.max('h2)) counter_1 (
    .Q(counter_1_q), .clk(or_1_out), .clr(comparator_2_eq));  // open: load, D, count, carry, up
  or or_1 (or_1_out, and_1_out, and_2_out, and_3_out);
  D_Flip_Flop d_ff_1 (.clk(clock_1_out), .Q(d_ff_1_q), .preset(Sc_out), .reset(d_ff_3_q[0]));  // open: D, Qn
  D_Flip_Flop d_ff_2 (.clk(clock_1_out), .Q(d_ff_2_q), .preset(Sp_out), .reset(d_ff_3_q[1]));  // open: D, Qn
  Comparator #(.width(16)) comparator_1 (
    .a({register_1_q_2, register_1_q}), .b(16'h3e8), .gt(comparator_1_gt), .eq(comparator_1_eq));  // open: lt
  or or_2 (or_2_out, comparator_1_eq, comparator_1_gt);
  LED led_1 (.in(or_2_out));
  Comparator comparator_2 (.a(counter_1_q), .b(8'h2), .eq(comparator_2_eq));  // open: gt, lt
  S_R_Flip_Flop s_r_ff_1 (.Q(s_r_ff_1_q), .reset(comparator_2_eq), .preset(comparator_5_eq));  // open: S, R, clk, Qn
  and and_1 (and_1_out, clock_1_out, s_r_ff_1_q);
  D_Flip_Flop d_ff_3 (.D(d_ff_1_q), .clk(clock_1_out), .Q(d_ff_3_q[0]));  // open: Qn, preset, reset
  D_Flip_Flop d_ff_4 (.D(d_ff_2_q), .clk(clock_1_out), .Q(d_ff_3_q[1]));  // open: Qn, preset, reset
  and and_2 (and_2_out, clock_1_out, rgbled_1_p2);
  // Probe on {register_1_q_2, register_1_q}
  // Probe on beverage_button_1_out_7
  Beverage_Button beverage_button_1 (
    .in_1({register_1_q_2, register_1_q}), .in_2(Ba_out), .in_3(Bb_out), .in_4(Bc_out), .in_5(clock_1_out),
    .in_6(or_5_out), .out_7(beverage_button_1_out_7), .out_8(beverage_button_1_out_8));
  Comparator #(.width(16)) comparator_3 (
    .a({register_1_q_2, register_1_q}), .b(16'h5dc), .gt(comparator_3_gt), .eq(comparator_3_eq));  // open: lt
  or or_3 (or_3_out, comparator_3_eq, comparator_3_gt);
  LED led_2 (.in(or_3_out));
  // RGBLED rgbled_1: pin names not known; wires that end beside it: s_r_ff_1_q, rgbled_1_p2, rgbled_1_p3
  S_R_Flip_Flop s_r_ff_2 (.Q(rgbled_1_p2), .reset(comparator_2_eq), .preset(comparator_6_eq));  // open: S, R, clk, Qn
  and and_3 (and_3_out, clock_1_out, rgbled_1_p3);
  Adder #(.width(16)) adder_1 (
    .a({register_1_q_2, register_1_q}), .b(multiplexer_3_out), .out(adder_1_out), .cin(1'b0));  // open: cout
  Subtractor #(.width(16)) subtractor_1 (
    .a({register_1_q_2, register_1_q}), .b(beverage_button_1_out_7), .out(subtractor_1_out), .bin(1'b0));  // open: bout
  Comparator #(.width(16)) comparator_4 (
    .a({register_1_q_2, register_1_q}), .b(16'h7d0), .gt(comparator_4_gt), .eq(comparator_4_eq));  // open: lt
  or or_4 (or_4_out, comparator_4_eq, comparator_4_gt);
  LED led_3 (.in(or_4_out));
  S_R_Flip_Flop s_r_ff_3 (.Q(rgbled_1_p3), .reset(comparator_2_eq), .preset(comparator_7_eq));  // open: S, R, clk, Qn
  Multiplexer #(.width(16)) multiplexer_1 (
    .in0(adder_1_out), .in1(subtractor_1_out), .out(multiplexer_1_out), .sel(beverage_button_1_out_8));
  or or_5 (or_5_out, d_ff_3_q[0], d_ff_3_q[1]);
  not not_1 (not_1_out, clock_1_out);
  Multiplexer #(.select(2), .width(16)) multiplexer_2 (
    .in0({16{1'b0}}), .in1(16'h1f4), .in2(16'h3e8), .out(multiplexer_2_out), .sel(d_ff_3_q));  // open: in3
  Comparator #(.width(16)) comparator_5 (
    .a(beverage_button_1_out_7), .b(16'h3e8), .eq(comparator_5_eq));  // open: gt, lt
  Register #(.width(16)) register_1 (
    .D(multiplexer_1_out), .en(not_1_out), .clk(clock_1_out), .Q({register_1_q_2, register_1_q}),
    .clr(button_1_out));
  Button button_1 (.out(button_1_out));
  Comparator #(.width(16)) comparator_6 (
    .a(beverage_button_1_out_7), .b(16'h5dc), .eq(comparator_6_eq));  // open: gt, lt
  Comparator #(.width(16)) comparator_7 (
    .a(beverage_button_1_out_7), .b(16'h7d0), .eq(comparator_7_eq));  // open: gt, lt
  Hex_Digit_Display hex_digit_display_1 ();  // open: value, dp
  // Binary_to_BCD_converter #(.binvalue(13)) binary_to_bcd_converter_1: pin names not known; wires that end beside it: register_1_q, multiplexer_1_out, {register_1_q_2, register_1_q}
  Comparator #(.width(16)) comparator_8 (.a(multiplexer_1_out), .b(16'h1388), .eq(comparator_8_eq));  // open: gt, lt
  Comparator #(.width(16)) comparator_9 (
    .a({register_1_q_2, register_1_q}), .b(16'h1194), .eq(comparator_9_eq));  // open: gt, lt
  Multiplexer #(.width(16)) multiplexer_3 (
    .in0(multiplexer_2_out), .in1({16{1'b0}}), .out(multiplexer_3_out), .sel(or_6_out));
  Hex_Digit_Display hex_digit_display_2 ();  // open: value, dp
  Hex_Digit_Display hex_digit_display_3 ();  // open: value, dp
  Comparator #(.width(16)) comparator_10 (.a(16'h3e8), .b(multiplexer_2_out), .eq(comparator_10_eq));  // open: gt, lt
  Hex_Digit_Display hex_digit_display_4 ();  // open: value, dp
  D_Flip_Flop d_ff_5 (.D(comparator_8_eq), .clk(clock_1_out), .Q(d_ff_5_q));  // open: Qn, preset, reset
  and and_4 (and_4_out, comparator_9_eq, comparator_10_eq);
  or or_6 (or_6_out, and_4_out, d_ff_5_q);
  Multiplexer #(.width(16)) multiplexer_4 (
    .in0({16{1'b0}}), .in1(multiplexer_2_out), .out(multiplexer_4_out), .sel(or_6_out));
  Hex_Digit_Display hex_digit_display_5 ();  // open: value, dp
  Hex_Digit_Display hex_digit_display_6 ();  // open: value, dp
  // Binary_to_BCD_converter #(.binvalue(13)) binary_to_bcd_converter_2: pin names not known; wires that end beside it: multiplexer_4_out[12:0]
  Hex_Digit_Display hex_digit_display_7 ();  // open: value, dp
  Hex_Digit_Display hex_digit_display_8 ();  // open: value, dp
endmodule

module Money_input (
  input  Sc,
  input  [15:0] RSTREG,
  input  Sp,
  output [15:0] value,
  output state
);

  wire button_1_out, comparator_1_gt, d_ff_1_q, d_ff_2_q;
  wire [1:0] and_1_out;

  Button button_1 (.out(button_1_out));
  Comparator #(.width(16)) comparator_1 (.a(RSTREG), .b({16{1'b0}}), .gt(comparator_1_gt));  // open: eq, lt
  D_Flip_Flop d_ff_1 (.Q(d_ff_1_q), .preset(Sc), .reset(comparator_1_gt));  // open: D, clk, Qn
  D_Flip_Flop d_ff_2 (.Q(d_ff_2_q), .preset(Sp), .reset(comparator_1_gt));  // open: D, clk, Qn
  and and_1 (and_1_out[0], 1'b1, d_ff_1_q);
  and and_2 (and_1_out[1], 1'b1, d_ff_2_q);
  Multiplexer #(.select(2), .width(16)) multiplexer_1 (
    .in0({16{1'b0}}), .in1(16'h1f4), .in2(16'h3e8), .out(value), .sel(and_1_out));  // open: in3
endmodule

module Beverage_Button (
  input  [15:0] in_1,
  input  in_2,
  input  in_3,
  input  in_4,
  input  in_5,
  input  in_6,
  output [15:0] out_7,
  output out_8
);

  wire and_1_out, and_2_out, and_3_out, comparator_1_eq, comparator_1_gt, comparator_2_eq, comparator_2_gt,
       comparator_3_eq, comparator_3_gt, d_ff_1_q, d_ff_2_q, d_ff_3_q, d_ff_4_q, d_ff_5_q, d_ff_6_q,
       or_1_out, or_2_out, or_3_out, or_4_out;
  wire [1:0] or_5_out;

  Comparator #(.width(16)) comparator_1 (
    .a(in_1), .b(16'h3e8), .gt(comparator_1_gt), .eq(comparator_1_eq));  // open: lt
  or or_1 (or_1_out, comparator_1_gt, comparator_1_eq);
  Comparator #(.width(16)) comparator_2 (
    .a(in_1), .b(16'h5dc), .gt(comparator_2_gt), .eq(comparator_2_eq));  // open: lt
  and and_1 (and_1_out, or_1_out, in_2);
  and and_2 (and_2_out, or_3_out, in_4);
  and and_3 (and_3_out, or_2_out, in_3);
  or or_2 (or_2_out, comparator_2_gt, comparator_2_eq);
  Comparator #(.width(16)) comparator_3 (
    .a(in_1), .b(16'h7d0), .gt(comparator_3_gt), .eq(comparator_3_eq));  // open: lt
  D_Flip_Flop d_ff_1 (.clk(in_5), .Q(d_ff_1_q), .preset(and_1_out), .reset(d_ff_4_q));  // open: D, Qn
  D_Flip_Flop d_ff_2 (.clk(in_5), .Q(d_ff_2_q), .preset(and_2_out), .reset(d_ff_5_q));  // open: D, Qn
  D_Flip_Flop d_ff_3 (.clk(in_5), .Q(d_ff_3_q), .preset(and_3_out), .reset(d_ff_6_q));  // open: D, Qn
  or or_3 (or_3_out, comparator_3_gt, comparator_3_eq);
  D_Flip_Flop d_ff_4 (.D(d_ff_1_q), .clk(in_5), .Q(d_ff_4_q));  // open: Qn, preset, reset
  D_Flip_Flop d_ff_5 (.D(d_ff_2_q), .clk(in_5), .Q(d_ff_5_q));  // open: Qn, preset, reset
  D_Flip_Flop d_ff_6 (.D(d_ff_3_q), .clk(in_5), .Q(d_ff_6_q));  // open: Qn, preset, reset
  or or_4 (or_4_out, in_2, in_4, in_3);
  or or_5 (or_5_out[0], d_ff_4_q, d_ff_5_q);
  or or_6 (or_5_out[1], d_ff_5_q, d_ff_6_q);
  ROM #(.addrWidth(2), .dataWidth(16)) rom_1 (.addr(or_5_out), .data(out_7));
  D_Flip_Flop d_ff_7 (.Q(out_8), .preset(or_4_out), .reset(in_6));  // open: D, clk, Qn

  // Notes on the sheet:
  //   contents of rom_1 (hex, n*v repeats v):
  //   0 3e8 5dc 7d0
endmodule
