// Logisim project vending_machine_ver6.circ as structural Verilog: 6 circuits, main circuit main
module main (
);

  wire Ba_out, balance_1_mode, Bb_out, Bc_out, clock_1_out, drink_1_mode_output, led_output_1_enable_1000,
       led_output_1_enable_1500, led_output_1_enable_2000, led_output_1_output_1000,
       led_output_1_output_1500, led_output_1_output_2000, money_1_add_mode, not_1_out, reset_out,
       return_money_out, Sc_out, Sp_out;
  wire [2:0] cir_logic_1_exceed_return_2, register_1_q_2;
  wire [7:0] balance_1_coin_cnt, balance_1_paper_cnt;
  wire [12:0] cir_logic_1_exceed_return, register_1_q;
  wire [15:0] balance_1_led, balance_1_value, cir_logic_1_accepted_money, cir_logic_1_value, drink_1_value,
       money_1_value, multiplexer_1_out;

  Button Ba (.out(Ba_out));
  Button Bb (.out(Bb_out));
  Button Bc (.out(Bc_out));
  Clock clock_1 (.out(clock_1_out));
  Button Sc (.out(Sc_out));
  Button Sp (.out(Sp_out));
  Button return_money (.out(return_money_out));
  Money money_1 (.Sc(Sc_out), .Sp(Sp_out), .clk(clock_1_out), .add_mode(money_1_add_mode), .value(money_1_value));
  Drink drink_1 (
    .memory({register_1_q_2, register_1_q}), .b_1000(Ba_out), .b_1500(Bb_out), .b_2000(Bc_out),
    .clk(clock_1_out), .add_mode(money_1_add_mode), .value(drink_1_value), .mode_output(drink_1_mode_output));
  // Probe on drink_1_value
  not not_1 (not_1_out, clock_1_out);
  Register #(.width(16)) register_1 (
    .D(multiplexer_1_out), .en(not_1_out), .clk(clock_1_out), .Q({register_1_q_2, register_1_q}),
    .clr(reset_out));
  Button reset (.out(reset_out));
  cir_logic cir_logic_1 (
    .memory_output({register_1_q_2, register_1_q}), .clk(clock_1_out), .mode_input(drink_1_mode_output),
    .money_input(money_1_value), .Drink_input(drink_1_value), .value(cir_logic_1_value),
    .accepted_money(cir_logic_1_accepted_money),
    .Exceed_Return({cir_logic_1_exceed_return_2, cir_logic_1_exceed_return}));
  Multiplexer #(.width(16)) multiplexer_1 (
    .in0(cir_logic_1_value), .in1(balance_1_value), .out(multiplexer_1_out), .sel(balance_1_mode));
  Balance balance_1 (
    .money_value(cir_logic_1_accepted_money), .clk(clock_1_out), .reset(reset_out),
    .memory({register_1_q_2, register_1_q}), .return_input(return_money_out), .coin_cnt(balance_1_coin_cnt),
    .paper_cnt(balance_1_paper_cnt), .value(balance_1_value), .led(balance_1_led), .mode(balance_1_mode));
  // Probe on {register_1_q_2, register_1_q}
  Hex_Digit_Display hex_digit_display_1 ();  // open: value, dp
  // Binary_to_BCD_converter #(.binvalue(13)) binary_to_bcd_converter_1: pin names not known; wires that end beside it: register_1_q
  Hex_Digit_Display hex_digit_display_2 ();  // open: value, dp
  // Binary_to_BCD_converter #(.binvalue(13)) binary_to_bcd_converter_2: pin names not known; wires that end beside it: cir_logic_1_exceed_return
  Hex_Digit_Display hex_digit_display_3 ();  // open: value, dp
  // Binary_to_BCD_converter #(.binvalue(13)) binary_to_bcd_converter_3: pin names not known; wires that end beside it: balance_1_led[12:0]
  Hex_Digit_Display hex_digit_display_4 ();  // open: value, dp
  // Binary_to_BCD_converter #(.binvalue(8)) binary_to_bcd_converter_4: pin names not known; wires that end beside it: balance_1_coin_cnt
  Hex_Digit_Display hex_digit_display_5 ();  // open: value, dp
  // Binary_to_BCD_converter #(.binvalue(8)) binary_to_bcd_converter_5: pin names not known; wires that end beside it: balance_1_paper_cnt
  LED_output led_output_1 (
    .memory_input({register_1_q_2, register_1_q}), .circulate_input(drink_1_value), .clk(clock_1_out),
    .enable_1000(led_output_1_enable_1000), .enable_1500(led_output_1_enable_1500),
    .enable_2000(led_output_1_enable_2000), .output_1000(led_output_1_output_1000),
    .output_1500(led_output_1_output_1500), .output_2000(led_output_1_output_2000));
  Hex_Digit_Display hex_digit_display_6 ();  // open: value, dp
  Hex_Digit_Display hex_digit_display_7 ();  // open: value, dp
  Hex_Digit_Display hex_digit_display_8 ();  // open: value, dp
  Hex_Digit_Display hex_digit_display_9 ();  // open: value, dp
  Hex_Digit_Display hex_digit_display_10 ();  // open: value, dp
  Hex_Digit_Display hex_digit_display_11 ();  // open: value, dp
  Hex_Digit_Display hex_digit_display_12 ();  // open: value, dp
  Hex_Digit_Display hex_digit_display_13 ();  // open: value, dp
  LED led_1 (.in(led_output_1_enable_1000));
  LED led_2 (.in(led_output_1_enable_1500));
  LED led_3 (.in(led_output_1_enable_2000));
  Hex_Digit_Display hex_digit_display_14 ();  // open: value, dp
  Hex_Digit_Display hex_digit_display_15 ();  // open: value, dp
  Hex_Digit_Display hex_digit_display_16 ();  // open: value, dp
  Hex_Digit_Display hex_digit_display_17 ();  // open: value, dp
  Hex_Digit_Display hex_digit_display_18 ();  // open: value, dp
  // RGBLED rgbled_1: pin names not known; wires that end beside it: led_output_1_enable_1000, led_output_1_output_1000, led_output_1_output_1500, led_output_1_output_2000
endmodule

module Money (
  input  Sc,
  input  Sp,
  input  clk,
  output add_mode,
  output [15:0] value
);

  wire d_ff_1_q, d_ff_2_q;
  wire [1:0] d_ff_3_q;

  D_Flip_Flop d_ff_1 (.clk(clk), .Q(d_ff_1_q), .preset(Sc), .reset(d_ff_3_q[0]));  // open: D, Qn
  D_Flip_Flop d_ff_2 (.clk(clk), .Q(d_ff_2_q), .preset(Sp), .reset(d_ff_3_q[1]));  // open: D, Qn
  D_Flip_Flop d_ff_3 (.D(d_ff_1_q), .clk(clk), .Q(d_ff_3_q[0]));  // open: Qn, preset, reset
  D_Flip_Flop d_ff_4 (.D(d_ff_2_q), .clk(clk), .Q(d_ff_3_q[1]));  // open: Qn, preset, reset
  or or_1 (add_mode, d_ff_3_q[0], d_ff_3_q[1]);
  Multiplexer #(.select(2), .width(16)) multiplexer_1 (
    .in0({16{1'b0}}), .in1(16'h1f4), .in2(16'h3e8), .out(value), .sel(d_ff_3_q));  // open: in3
endmodule

module Drink (
  input  [15:0] memory,
  input  b_1000,
  input  b_1500,
  input  b_2000,
  input  clk,
  input  add_mode,
  output [15:0] value,
  output mode_output
);

  wire and_1_out, and_2_out, and_3_out, comparator_1_eq, comparator_1_gt, comparator_2_eq, comparator_2_gt,
       comparator_3_eq, comparator_3_gt, d_ff_1_q, d_ff_2_q, d_ff_3_q, d_ff_4_q, d_ff_5_q, d_ff_6_q,
       or_1_out, or_2_out, or_3_out, or_4_out;
  wire [1:0] or_5_out;

  Comparator #(.width(16)) comparator_1 (
    .a(memory), .b(16'h3e8), .gt(comparator_1_gt), .eq(comparator_1_eq));  // open: lt
  Comparator #(.width(16)) comparator_2 (
    .a(memory), .b(16'h5dc), .gt(comparator_2_gt), .eq(comparator_2_eq));  // open: lt
  or or_1 (or_1_out, comparator_1_gt, comparator_1_eq);
  and and_1 (and_1_out, or_1_out, b_1000);
  and and_2 (and_2_out, or_3_out, b_2000);
  and and_3 (and_3_out, or_2_out, b_1500);
  D_Flip_Flop d_ff_1 (.clk(clk), .Q(d_ff_1_q), .preset(and_3_out), .reset(d_ff_6_q));  // open: D, Qn
  or or_2 (or_2_out, comparator_2_gt, comparator_2_eq);
  Comparator #(.width(16)) comparator_3 (
    .a(memory), .b(16'h7d0), .gt(comparator_3_gt), .eq(comparator_3_eq));  // open: lt
  D_Flip_Flop d_ff_2 (.clk(clk), .Q(d_ff_2_q), .preset(and_1_out), .reset(d_ff_4_q));  // open: D, Qn
  D_Flip_Flop d_ff_3 (.clk(clk), .Q(d_ff_3_q), .preset(and_2_out), .reset(d_ff_5_q));  // open: D, Qn
  or or_3 (or_3_out, comparator_3_gt, comparator_3_eq);
  D_Flip_Flop d_ff_4 (.D(d_ff_2_q), .clk(clk), .Q(d_ff_4_q));  // open: Qn, preset, reset
  D_Flip_Flop d_ff_5 (.D(d_ff_3_q), .clk(clk), .Q(d_ff_5_q));  // open: Qn, preset, reset
  D_Flip_Flop d_ff_6 (.D(d_ff_1_q), .clk(clk), .Q(d_ff_6_q));  // open: Qn, preset, reset
  or or_4 (or_4_out, b_1000, b_2000, b_1500);
  or or_5 (or_5_out[0], d_ff_4_q, d_ff_5_q);
  or or_6 (or_5_out[1], d_ff_5_q, d_ff_6_q);
  ROM #(.addrWidth(2), .dataWidth(16)) rom_1 (.addr(or_5_out), .data(value));
  D_Flip_Flop cir_mode (.Q(mode_output), .preset(or_4_out), .reset(add_mode));  // open: D, clk, Qn

  // Notes on the sheet:
  //   contents of rom_1 (hex, n*v repeats v):
  //   0 3e8 5dc 7d0
endmodule

module LED_output (
  input  [15:0] memory_input,
  input  [15:0] circulate_input,
  input  clk,
  output enable_1000,
  output enable_1500,
  output enable_2000,
  output output_1000,
  output output_1500,
  output output_2000
);

  wire and_1_out, and_2_out, and_3_out, comparator_1_eq, comparator_1_gt, comparator_2_eq, comparator_3_eq,
       comparator_3_gt, comparator_4_eq, comparator_5_eq, comparator_5_gt, comparator_6_eq, comparator_7_eq,
       or_1_out;
  wire [7:0] counter_1_q;

  Comparator #(.width(16)) comparator_1 (
    .a(memory_input), .b(16'h3e8), .gt(comparator_1_gt), .eq(comparator_1_eq));  // open: lt
  Counter #(.max('h2)) counter_1 (
    .Q(counter_1_q), .clk(or_1_out), .clr(comparator_2_eq));  // open: load, D, count, carry, up
  or or_1 (or_1_out, and_1_out, and_2_out, and_3_out);
  or or_2 (enable_1000, comparator_1_eq, comparator_1_gt);
  Comparator comparator_2 (.a(counter_1_q), .b(8'h2), .eq(comparator_2_eq));  // open: gt, lt
  S_R_Flip_Flop s_r_ff_1 (.Q(output_1000), .reset(comparator_2_eq), .preset(comparator_4_eq));  // open: S, R, clk, Qn
  and and_1 (and_1_out, clk, output_1000);
  and and_2 (and_2_out, clk, output_1500);
  Comparator #(.width(16)) comparator_3 (
    .a(memory_input), .b(16'h5dc), .gt(comparator_3_gt), .eq(comparator_3_eq));  // open: lt
  Comparator #(.width(16)) comparator_4 (.a(circulate_input), .b(16'h3e8), .eq(comparator_4_eq));  // open: gt, lt
  and and_3 (and_3_out, clk, output_2000);
  or or_3 (enable_1500, comparator_3_eq, comparator_3_gt);
  S_R_Flip_Flop s_r_ff_2 (.Q(output_1500), .reset(comparator_2_eq), .preset(comparator_6_eq));  // open: S, R, clk, Qn
  Comparator #(.width(16)) comparator_5 (
    .a(memory_input), .b(16'h7d0), .gt(comparator_5_gt), .eq(comparator_5_eq));  // open: lt
  Comparator #(.width(16)) comparator_6 (.a(circulate_input), .b(16'h5dc), .eq(comparator_6_eq));  // open: gt, lt
  or or_4 (enable_2000, comparator_5_eq, comparator_5_gt);
  Comparator #(.width(16)) comparator_7 (.a(circulate_input), .b(16'h7d0), .eq(comparator_7_eq));  // open: gt, lt
  S_R_Flip_Flop s_r_ff_3 (.Q(output_2000), .reset(comparator_2_eq), .preset(comparator_7_eq));  // open: S, R, clk, Qn
endmodule

module cir_logic (
  input  [15:0] memory_output,
  input  clk,
  input  mode_input,
  input  [15:0] money_input,
  input  [15:0] Drink_input,
  output [15:0] value,
  output [15:0] accepted_money,
  output [15:0] Exceed_Return
);

  wire and_1_out, comparator_1_eq, comparator_2_eq, comparator_3_eq, d_ff_1_q, or_1_out;
  wire [15:0] adder_1_out, subtractor_1_out;

  Multiplexer #(.width(16)) multiplexer_1 (.in0(money_input), .in1({16{1'b0}}), .out(accepted_money), .sel(or_1_out));
  Adder #(.width(16)) adder_1 (.a(memory_output), .b(accepted_money), .out(adder_1_out), .cin(1'b0));  // open: cout
  Subtractor #(.width(16)) subtractor_1 (
    .a(memory_output), .b(Drink_input), .out(subtractor_1_out), .bin(1'b0));  // open: bout
  Multiplexer #(.width(16)) multiplexer_2 (.in0(adder_1_out), .in1(subtractor_1_out), .out(value), .sel(mode_input));
  Comparator #(.width(16)) comparator_1 (.a(value), .b(16'h1388), .eq(comparator_1_eq));  // open: gt, lt
  Comparator #(.width(16)) comparator_2 (.a(memory_output), .b(16'h1194), .eq(comparator_2_eq));  // open: gt, lt
  Comparator #(.width(16)) comparator_3 (.a(16'h3e8), .b(money_input), .eq(comparator_3_eq));  // open: gt, lt
  D_Flip_Flop d_ff_1 (.D(comparator_1_eq), .clk(clk), .Q(d_ff_1_q));  // open: Qn, preset, reset
  and and_1 (and_1_out, comparator_2_eq, comparator_3_eq);
  or or_1 (or_1_out, and_1_out, d_ff_1_q);
  Multiplexer #(.width(16)) multiplexer_3 (.in0({16{1'b0}}), .in1(money_input), .out(Exceed_Return), .sel(or_1_out));
endmodule

module Balance (
  input  [15:0] money_value,
  input  clk,
  input  reset,
  input  [15:0] memory,
  input  return_input,
  output [7:0] coin_cnt,
  output [7:0] paper_cnt,
  output [15:0] value,
  output [15:0] led,
  output mode
);

  wire and_1_out, and_2_out, and_5_out, comparator_1_eq, comparator_2_eq, comparator_2_gt, comparator_2_lt,
       comparator_3_eq, comparator_3_gt, comparator_4_eq, comparator_5_eq, comparator_6_eq, comparator_7_eq,
       comparator_7_gt, comparator_8_eq, comparator_8_gt, comparator_9_eq, comparator_9_gt, if_paper_0_out,
       not_1_out, not_2_out, or_1_out, or_2_out, or_3_out, or_4_out, or_5_out, paper_priority_q;
  wire [1:0] and_3_out;
  wire [15:0] divider_1_out, divider_1_rem;

  Comparator #(.width(16)) comparator_1 (.a(money_value), .b(16'h1f4), .eq(comparator_1_eq));  // open: gt, lt
  Comparator #(.width(16)) comparator_2 (
    .a(memory), .b(16'h3e8), .gt(comparator_2_gt), .eq(comparator_2_eq), .lt(comparator_2_lt));
  Comparator #(.width(16)) comparator_3 (
    .a(memory), .b({16{1'b0}}), .gt(comparator_3_gt), .eq(comparator_3_eq));  // open: lt
  Comparator #(.width(16)) comparator_4 (.a(money_value), .b(16'h3e8), .eq(comparator_4_eq));  // open: gt, lt
  or or_1 (or_1_out, comparator_1_eq, comparator_9_eq);
  or or_2 (or_2_out, comparator_2_gt, comparator_2_eq);
  Divider #(.width(16)) divider_1 (.a(memory), .b(16'h3e8), .out(divider_1_out), .rem(divider_1_rem));  // open: upper
  Counter coin_counter (
    .count(or_1_out), .Q(coin_cnt), .up(not_1_out), .clk(clk), .clr(reset));  // open: load, D, carry
  D_Flip_Flop paper_priority (.Q(paper_priority_q), .preset(or_2_out), .reset(comparator_2_lt));  // open: D, clk, Qn
  and and_1 (and_1_out, comparator_3_gt, return_input);
  D_Flip_Flop return_mode (.Q(mode), .preset(and_1_out), .reset(or_3_out));  // open: D, clk, Qn
  or or_3 (or_3_out, comparator_3_eq, if_paper_0_out, and_5_out);
  and if_paper_0 (if_paper_0_out, comparator_5_eq, and_2_out);
  Comparator #(.width(16)) comparator_5 (.a(divider_1_out), .b({16{1'b0}}), .eq(comparator_5_eq));  // open: gt, lt
  Comparator #(.width(16)) comparator_6 (.a(divider_1_rem), .b(16'h1f4), .eq(comparator_6_eq));  // open: gt, lt
  or or_4 (or_4_out, comparator_4_eq, comparator_9_gt);
  and and_2 (and_2_out, comparator_6_eq, comparator_7_eq);
  not not_1 (not_1_out, mode);
  Counter paper_counter (
    .count(or_4_out), .Q(paper_cnt), .up(not_1_out), .clk(clk), .clr(reset));  // open: load, D, carry
  Comparator #(.mode("unsigned")) comparator_7 (
    .a(coin_cnt), .b({8{1'b0}}), .gt(comparator_7_gt), .eq(comparator_7_eq));  // open: lt
  Comparator #(.mode("unsigned")) comparator_8 (
    .a(paper_cnt), .b({8{1'b0}}), .gt(comparator_8_gt), .eq(comparator_8_eq));  // open: lt
  or or_5 (or_5_out, comparator_8_eq, not_2_out);
  not not_2 (not_2_out, paper_priority_q);
  and and_3 (and_3_out[0], comparator_8_gt, mode, paper_priority_q);
  and and_4 (and_3_out[1], comparator_7_gt, mode, or_5_out);
  and and_5 (and_5_out, comparator_8_eq, mode, comparator_7_eq);
  Multiplexer #(.select(2), .width(16)) multiplexer_1 (
    .in0({16{1'b0}}), .in1(16'h3e8), .in2(16'h1f4), .out(led), .sel(and_3_out));  // open: in3
  Subtractor #(.width(16)) subtractor_1 (.a(memory), .b(led), .out(value), .bin(1'b0));  // open: bout
  Comparator #(.width(16)) comparator_9 (.a(led), .b(16'h1f4), .gt(comparator_9_gt), .eq(comparator_9_eq));  // open: lt
endmodule
